// Logisim project Ejercicio24.circ as structural Verilog: 1 circuit, main circuit main
module main (
  input  x,
  input  y,
  input  CLK,
  output w
);

  wire and_1_out, and_2_out, carry_q, or_1_out, xor_1_out;

  xor xor_1 (xor_1_out, x, y);
  and and_1 (and_1_out, x, y);
  xor xor_2 (w, carry_q, xor_1_out);
  and and_2 (and_2_out, carry_q, xor_1_out);
  or or_1 (or_1_out, and_2_out, and_1_out);
  D_Flip_Flop carry (.D(or_1_out), .clk(CLK), .Q(carry_q));  // open: Qn, preset, reset
endmodule
