// Logisim project ejercicio13.circ as structural Verilog: 1 circuit, main circuit main
module main (
  input  madera,
  input  CLK,
  output cortar
);

  wire and_1_out, and_2_out, d_ff_1_q, d_ff_2_q, not_1_out, xor_1_out;

  not not_1 (not_1_out, d_ff_2_q);
  xor xor_1 (xor_1_out, d_ff_1_q, d_ff_2_q);
  and and_1 (and_1_out, xor_1_out, madera);
  and and_2 (and_2_out, madera, not_1_out);
  D_Flip_Flop d_ff_1 (.D(and_1_out), .clk(CLK), .Q(d_ff_1_q));  // open: Qn, preset, reset
  D_Flip_Flop d_ff_2 (.D(and_2_out), .clk(CLK), .Q(d_ff_2_q));  // open: Qn, preset, reset
  and and_3 (cortar, d_ff_1_q, d_ff_2_q);
endmodule
