// Logisim project practica1.circ as structural Verilog: 4 circuits, main circuit desarrollo1
module desarrollo1 (
  input  in_1,
  input  in_2,
  output out_3,
  output out_4,
  output out_5
);

  and and_1 (out_3, in_2, in_1);
  or or_1 (out_4, in_2, in_1);
  not not_1 (out_5, in_2);
endmodule

module desarrollo2 (
  input  [7:0] in_1,
  output X,
  output Y,
  output Z
);

  not not_1 (X, in_1[4]);
  or or_1 (Y, in_1[3], in_1[6]);
  and and_1 (Z, in_1[6], in_1[7]);
endmodule

module XOR1B (
  input  in_1,
  input  in_2,
  output out_3
);

  wire and_1_out, and_2_out, not_1_out, not_2_out;

  not not_1 (not_1_out, in_1);
  not not_2 (not_2_out, in_2);
  and and_1 (and_1_out, not_1_out, in_2);
  and and_2 (and_2_out, not_2_out, in_1);
  or or_1 (out_3, and_1_out, and_2_out);
endmodule

module XOR8B (
  input  [7:0] in_1,
  input  [7:0] in_2
);

  wire xor1b_1_out_3, xor1b_2_out_3, xor1b_3_out_3, xor1b_4_out_3;

  XOR1B xor1b_1 (.in_2(in_2[0]), .in_1(in_1[0]), .out_3(xor1b_1_out_3));
  XOR1B xor1b_2 (.in_2(in_2[1]), .in_1(in_1[1]), .out_3(xor1b_2_out_3));
  XOR1B xor1b_3 (.in_2(in_2[2]), .in_1(in_1[2]), .out_3(xor1b_3_out_3));
  XOR1B xor1b_4 (.in_2(in_2[3]), .in_1(in_1[3]), .out_3(xor1b_4_out_3));
  XOR1B xor1b_5 (.in_2(in_2[4]), .in_1(in_1[4]));  // open: out_3
  XOR1B xor1b_6 (.in_2(in_2[5]), .in_1(in_1[5]));  // open: out_3
  XOR1B xor1b_7 (.in_2(in_2[6]), .in_1(in_1[6]));  // open: out_3
  XOR1B xor1b_8 (.in_2(in_2[7]), .in_1(in_1[7]));  // open: out_3
endmodule
